# Fritzing sketch frizing-design (saved by Fritzing 0.9.3b)
circuit board: 4.86829cm x 5.63974cm
breadboards: 1

parts:
  R1 = PHOTOCELL [package=photocell-kit]
  R2 = Resistor [tolerance=±5% resistance=10k package=THT]
  R3 = Resistor [tolerance=±5% resistance=220 package=THT]
  R4 = Resistor [tolerance=±5% resistance=220 package=THT]
  R5 = Resistor [tolerance=±5% resistance=220 package=THT]
  R6 = Resistor [tolerance=±5% resistance=220 package=THT]
  LED1 = LED - 5mm [color="Red (633nm)" package="5 mm [THT]"]
  LED2 = LED - 5mm [color="Blue (430nm)" package="5 mm [THT]"]
  LED3 = LED - 5mm [color="Yellow (585nm)" package="5 mm [THT]"]
  LED4 = LED - 5mm [color="Red (633nm)" package="5 mm [THT]"]
  R7 = Resistor [tolerance=±5% resistance=10k package=THT]
  S1 = Pushbutton [package="[THT]"]
  hc-sr1 = hc-sr04
  Teensy_3_1 = Teensy 3.0
  R9 = Resistor [tolerance=±5% resistance=220 package=THT]
  R10 = Resistor [tolerance=±5% resistance=100 package=THT]
  MCU1 = Raspberry Pi Zero

nets:
  N1: R1.P$1, R2.Pin_0, Teensy_3_1.A0/D14
  GND: R1.P$2, R3.Pin_1, R4.Pin_1, R5.Pin_1, R6.Pin_1, R7.Pin_1, hc-sr1.GND, Teensy_3_1.GND, R10.Pin_1, MCU1.pin_14, MCU1.pin_34, MCU1.pin_39
  N2: R2.Pin_1, S1.Pin_3, S1.Pin_4, Teensy_3_1.3V3, R9.Pin_0
  N3: R3.Pin_0, LED1.cathode
  N4: R4.Pin_0, LED2.cathode
  N5: R5.Pin_0, LED3.cathode
  N6: R6.Pin_0, LED4.cathode
  N7: LED1.anode, Teensy_3_1.D7
  N8: LED2.anode, Teensy_3_1.D6
  N9: LED3.anode, Teensy_3_1.D11
  N10: LED4.anode, Teensy_3_1.D3
  N11: R7.Pin_0, S1.Pin_1, S1.Pin_2, Teensy_3_1.D2, Teensy_3_1.D10
  VCC: hc-sr1.VCC, Teensy_3_1.Vin, MCU1.pin_2, MCU1.pin_4
  N12: hc-sr1.Trig, Teensy_3_1.A8/D22
  N13: hc-sr1.Echo, Teensy_3_1.A9/D23
  N14: Teensy_3_1.D0, MCU1.pin_8
  N15: Teensy_3_1.D1, MCU1.pin_10
  N16: Teensy_3_1.A2/D16, R9.Pin_1, R10.Pin_0
